# Fritzing sketch IRLibrary (saved by Fritzing 0.9.3b)

parts:
  Microcontroller = Arduino Uno (Rev3)
  R1 = Resistor [tolerance=±5% resistance=470 package=THT]
  IR_Receiver = TSOP312.., 314.. [package=THT]
  IR_Diode = LTE-302 [package=lte-302]
  LED1 = RGB LED (com. anode, rbg) [package="5 mm [THT]"]
  Q2 = NPN-Transistor [package="TO92 [THT]"]
  Part2 = LilyPad Slide Switch
  Part3 = LilyPad Slide Switch
  Part4 = LilyPad Slide Switch
  R2 = Resistor [tolerance=±5% resistance=330 package=THT]

nets:
  N1: Microcontroller.A0, LED1.red_cathode, Part4.ON
  N2: Microcontroller.A1, LED1.green_cathode, Part2.ON
  N3: Microcontroller.A2, LED1.blue_cathode, Part3.ON
  GND: Microcontroller.GND, IR_Receiver.GND, Q2.E, Part2.OFF, Part3.OFF, Part4.OFF
  N4: Microcontroller.D2, IR_Receiver.Data
  N5: Microcontroller.D3_PWM, R1.Pin_0
  N6: Microcontroller.5V, IR_Receiver.Vs, IR_Diode.A, R2.Pin_0
  N7: R1.Pin_1, Q2.B
  N8: IR_Diode.C, Q2.C
  N9: LED1.common_anode, R2.Pin_1
